// Logisim project alu.circ as structural Verilog: 2 circuits, main circuit alu
module alu (
  input  [31:0] A,
  input  [31:0] B,
  input  [3:0] ALUSel,
  output [31:0] Result
);

  wire comparator_1_lt;
  wire [31:0] add0, and0, divu, mul0, mulh0, mulhu, or0, remu, sll0, slt0, sra0, srl0, sub0, xor0;

  Adder #(.width(32)) adder_1 (.a(A), .b(B), .out(add0));  // open: cin, cout
  assign and0 = A & B;  // AND_Gate and_1, 32 bits wide
  assign or0 = A | B;  // OR_Gate or_1, 32 bits wide
  assign xor0 = A ^ B;  // XOR_Gate xor_1, 32 bits wide
  Shifter #(.width(32), .shift("lr")) shifter_1 (.in(A), .\dist (B[4:0]), .out(srl0));
  Shifter #(.width(32), .shift("ar")) shifter_2 (.in(A), .\dist (B[4:0]), .out(sra0));
  Shifter #(.width(32)) shifter_3 (.in(A), .\dist (B[4:0]), .out(sll0));
  Comparator #(.width(32)) comparator_1 (.a(A), .b(B), .lt(comparator_1_lt));  // open: gt, eq
  assign slt0 = {{31{1'b0}}, comparator_1_lt};  // Bit_Extender bit_extender_1
  Divider #(.width(32)) divider_1 (.a(A), .b(B), .out(divu));  // open: upper, rem
  Divider #(.width(32)) divider_2 (.a(A), .b(B), .rem(remu));  // open: out, upper
  Multiplier #(.width(32)) multiplier_1 (.a(A), .b(B), .out(mul0));  // open: cin, cout
  Multiplier #(.width(32)) multiplier_2 (.a(A), .b(B), .cout(mulhu));  // open: out, cin
  Subtractor #(.width(32)) subtractor_1 (.a(A), .b(B), .out(sub0));  // open: bin, bout
  mulhmod mulhmod_1 (.A(A), .B(B), .Result(mulh0));
  Multiplexer #(.select(4), .width(32), .enable("false")) multiplexer_1 (
    .in0(add0), .in1(and0), .in2(or0), .in3(xor0), .in4(srl0), .in5(sra0), .in6(sll0), .in7(slt0),
    .in8(divu), .in9(remu), .in10(mul0), .in11(mulhu), .in12(sub0), .in13(B), .in14(mulh0), .out(Result),
    .sel(ALUSel));  // open: in15

  // Other names for the same wires on the sheet: bsel[31:0] = B

  // Notes on the sheet:
  //   INPUTS to your circuit
  //   DON'T CHANGE THE LOCATIONS OF THE INPUTS AND OUTPUTS!
  //   OUTPUT from your circuit
endmodule

module mulhmod (
  input  [31:0] A,
  input  [31:0] B,
  output [31:0] Result
);

  wire adder_1_cout, subtractor_1_bout, subtractor_3_bout;
  wire [31:0] bit_extender_1_out, bit_extender_2_out, multiplier_1_cout, multiplier_1_out, multiplier_2_cout,
       multiplier_2_out, multiplier_3_cout, multiplier_3_out, multiplier_4_cout, multiplier_4_out,
       subtractor_1_out, subtractor_2_out, subtractor_3_out, subtractor_4_out;

  assign bit_extender_1_out = {{1{1'b0}}, A[30:0]};  // Bit_Extender bit_extender_1
  assign bit_extender_2_out = {{1{1'b0}}, B[30:0]};  // Bit_Extender bit_extender_2
  Multiplier #(.width(32)) multiplier_1 (
    .a(bit_extender_1_out), .b(bit_extender_2_out), .out(multiplier_1_out), .cout(multiplier_1_cout));  // open: cin
  Multiplier #(.width(32)) multiplier_2 (
    .a({A[31], {31{1'b0}}}), .b(bit_extender_2_out), .out(multiplier_2_out), .cout(multiplier_2_cout));  // open: cin
  Multiplier #(.width(32)) multiplier_3 (
    .a(bit_extender_1_out), .b({B[31], {31{1'b0}}}), .out(multiplier_3_out), .cout(multiplier_3_cout));  // open: cin
  Multiplier #(.width(32)) multiplier_4 (
    .a({A[31], {31{1'b0}}}), .b({B[31], {31{1'b0}}}), .out(multiplier_4_out), .cout(multiplier_4_cout));  // open: cin
  Subtractor #(.width(32)) subtractor_1 (
    .a(multiplier_1_out), .b(multiplier_2_out), .out(subtractor_1_out), .bout(subtractor_1_bout));  // open: bin
  Subtractor #(.width(32)) subtractor_2 (
    .a(multiplier_1_cout), .b(multiplier_2_cout), .out(subtractor_2_out), .bin(subtractor_1_bout));  // open: bout
  Subtractor #(.width(32)) subtractor_3 (
    .a(subtractor_1_out), .b(multiplier_3_out), .out(subtractor_3_out), .bout(subtractor_3_bout));  // open: bin
  Subtractor #(.width(32)) subtractor_4 (
    .a(subtractor_2_out), .b(multiplier_3_cout), .out(subtractor_4_out), .bin(subtractor_3_bout));  // open: bout
  Adder #(.width(32)) adder_1 (.a(subtractor_3_out), .b(multiplier_4_out), .cout(adder_1_cout));  // open: out, cin
  Adder #(.width(32)) adder_2 (
    .a(subtractor_4_out), .b(multiplier_4_cout), .out(Result), .cin(adder_1_cout));  // open: cout
endmodule
