// Logisim project control_logic.circ as structural Verilog: 10 circuits, main circuit control_logic
module control_logic (
  input  [31:0] inst,
  input  BrEq,
  input  BrLt,
  output PCSel,
  output RegWEn,
  output [2:0] ImmSel,
  output BrUn,
  output ASel,
  output BSel,
  output [3:0] ALUSel,
  output MemRW,
  output [1:0] WBSel
);

  wire comparator_1_eq, comparator_2_eq, comparator_3_eq, comparator_4_eq, comparator_5_eq, comparator_6_eq,
       comparator_7_eq, comparator_8_eq, comparator_9_eq, comparator_10_eq;
  wire [3:0] priority_encoder_1_out;
  wire [14:0] itype_logic_1_out_2, jalr_logic_1_out_1, litype_logic_1_out_2, rtype_logic_1_out_2,
       sbtype_logic_1_out_4, stype_logic_1_out_4, u1type_logic_1_out_1, u2type_logic_1_out_1,
       ujtype_logic_1_out_1;

  Comparator #(.width(7), .mode("unsigned")) comparator_1 (
    .a(inst[6:0]), .b(7'b0110011), .eq(comparator_1_eq));  // open: gt, lt
  Comparator #(.width(7), .mode("unsigned")) comparator_2 (
    .a(inst[6:0]), .b(7'b0000011), .eq(comparator_2_eq));  // open: gt, lt
  Comparator #(.width(7), .mode("unsigned")) comparator_3 (
    .a(inst[6:0]), .b(7'b0010011), .eq(comparator_3_eq));  // open: gt, lt
  Comparator #(.width(7), .mode("unsigned")) comparator_4 (
    .a(inst[6:0]), .b(7'b0100011), .eq(comparator_4_eq));  // open: gt, lt
  Comparator #(.width(7), .mode("unsigned")) comparator_5 (
    .a(inst[6:0]), .b(7'b1100011), .eq(comparator_5_eq));  // open: gt, lt
  Comparator #(.width(7), .mode("unsigned")) comparator_6 (
    .a(inst[6:0]), .b(7'b0010111), .eq(comparator_6_eq));  // open: gt, lt
  Comparator #(.width(7), .mode("unsigned")) comparator_7 (
    .a(inst[6:0]), .b(7'b0110111), .eq(comparator_7_eq));  // open: gt, lt
  Comparator #(.width(7), .mode("unsigned")) comparator_8 (
    .a(inst[6:0]), .b(7'b1101111), .eq(comparator_8_eq));  // open: gt, lt
  Comparator #(.width(7), .mode("unsigned")) comparator_9 (
    .a(inst[6:0]), .b(7'b1100111), .eq(comparator_9_eq));  // open: gt, lt
  Comparator #(.width(32), .mode("unsigned")) comparator_10 (
    .a(inst), .b({32{1'b0}}), .eq(comparator_10_eq));  // open: gt, lt
  Priority_Encoder #(.select(4)) priority_encoder_1 (
    .in0(comparator_1_eq), .in1(comparator_2_eq), .in2(comparator_3_eq), .in3(comparator_4_eq),
    .in4(comparator_5_eq), .in5(comparator_6_eq), .in6(comparator_7_eq), .in7(comparator_8_eq),
    .in8(comparator_9_eq), .in9(comparator_10_eq), .out(priority_encoder_1_out));  // open: in10, in11, in12, in13, in14, in15
  Rtype_logic rtype_logic_1 (.inst(inst), .out_2(rtype_logic_1_out_2));
  LItype_logic litype_logic_1 (.in_1(inst), .out_2(litype_logic_1_out_2));
  Itype_logic itype_logic_1 (.in_1(inst), .out_2(itype_logic_1_out_2));
  Stype_logic stype_logic_1 (.in_1(inst), .in_2(BrEq), .in_3(BrLt), .out_4(stype_logic_1_out_4));
  SBtype_logic sbtype_logic_1 (.in_1(inst), .in_2(BrEq), .in_3(BrLt), .out_4(sbtype_logic_1_out_4));
  U1type_logic u1type_logic_1 (.out_1(u1type_logic_1_out_1));
  U2type_logic u2type_logic_1 (.out_1(u2type_logic_1_out_1));
  UJtype_logic ujtype_logic_1 (.out_1(ujtype_logic_1_out_1));
  jalr_logic jalr_logic_1 (.out_1(jalr_logic_1_out_1));
  Multiplexer #(.select(4), .width(15), .enable("false")) multiplexer_1 (
    .in0(rtype_logic_1_out_2), .in1(litype_logic_1_out_2), .in2(itype_logic_1_out_2),
    .in3(stype_logic_1_out_4), .in4(sbtype_logic_1_out_4), .in5(u1type_logic_1_out_1),
    .in6(u2type_logic_1_out_1), .in7(ujtype_logic_1_out_1), .in8(jalr_logic_1_out_1), .in9({15{1'b0}}),
    .out({WBSel, MemRW, ALUSel, BSel, ASel, BrUn, ImmSel, RegWEn, PCSel}), .sel(priority_encoder_1_out));  // open: in10, in11, in12, in13, in14, in15

  // Notes on the sheet:
  //   INPUTS to your circuit
  //   DON'T CHANGE THE LOCATIONS OF THE INPUTS AND OUTPUTS!
  //   OUTPUT from your circuit
endmodule

module Rtype_logic (
  input  [31:0] inst,
  output [14:0] out_2
);

  wire comparator_1_eq, comparator_2_eq, comparator_3_eq, comparator_4_eq, comparator_5_eq, comparator_6_eq,
       comparator_7_eq, comparator_8_eq, comparator_9_eq, comparator_10_eq, comparator_11_eq,
       comparator_12_eq, comparator_13_eq, comparator_14_eq;

  Comparator #(.width(10), .mode("unsigned")) comparator_1 (
    .a({inst[31:25], inst[14:12]}), .b({10{1'b0}}), .eq(comparator_1_eq));  // open: gt, lt
  Comparator #(.width(10), .mode("unsigned")) comparator_2 (
    .a({inst[31:25], inst[14:12]}), .b(10'h7), .eq(comparator_2_eq));  // open: gt, lt
  Comparator #(.width(10), .mode("unsigned")) comparator_3 (
    .a({inst[31:25], inst[14:12]}), .b(10'h6), .eq(comparator_3_eq));  // open: gt, lt
  Comparator #(.width(10), .mode("unsigned")) comparator_4 (
    .a({inst[31:25], inst[14:12]}), .b(10'h4), .eq(comparator_4_eq));  // open: gt, lt
  Comparator #(.width(10), .mode("unsigned")) comparator_5 (
    .a({inst[31:25], inst[14:12]}), .b(10'h5), .eq(comparator_5_eq));  // open: gt, lt
  Comparator #(.width(10), .mode("unsigned")) comparator_6 (
    .a({inst[31:25], inst[14:12]}), .b(10'h101), .eq(comparator_6_eq));  // open: gt, lt
  Comparator #(.width(10), .mode("unsigned")) comparator_7 (
    .a({inst[31:25], inst[14:12]}), .b(10'h1), .eq(comparator_7_eq));  // open: gt, lt
  Comparator #(.width(10), .mode("unsigned")) comparator_8 (
    .a({inst[31:25], inst[14:12]}), .b(10'h2), .eq(comparator_8_eq));  // open: gt, lt
  Comparator #(.width(10), .mode("unsigned")) comparator_9 (
    .a({inst[31:25], inst[14:12]}), .b(10'hd), .eq(comparator_9_eq));  // open: gt, lt
  Comparator #(.width(10), .mode("unsigned")) comparator_10 (
    .a({inst[31:25], inst[14:12]}), .b(10'hf), .eq(comparator_10_eq));  // open: gt, lt
  Comparator #(.width(10), .mode("unsigned")) comparator_11 (
    .a({inst[31:25], inst[14:12]}), .b(10'h8), .eq(comparator_11_eq));  // open: gt, lt
  Comparator #(.width(10), .mode("unsigned")) comparator_12 (
    .a({inst[31:25], inst[14:12]}), .b(10'h11), .eq(comparator_12_eq));  // open: gt, lt
  Comparator #(.width(10), .mode("unsigned")) comparator_13 (
    .a({inst[31:25], inst[14:12]}), .b(10'h100), .eq(comparator_13_eq));  // open: gt, lt
  Comparator #(.width(10), .mode("unsigned")) comparator_14 (
    .a({inst[31:25], inst[14:12]}), .b(10'h9), .eq(comparator_14_eq));  // open: gt, lt
  Priority_Encoder #(.select(4)) priority_encoder_1 (
    .in0(comparator_1_eq), .in1(comparator_2_eq), .in2(comparator_3_eq), .in3(comparator_4_eq),
    .in4(comparator_5_eq), .in5(comparator_6_eq), .in6(comparator_7_eq), .in7(comparator_8_eq),
    .in8(comparator_9_eq), .in9(comparator_10_eq), .in10(comparator_11_eq), .in11(comparator_12_eq),
    .in12(comparator_13_eq), .in14(comparator_14_eq), .out(out_2[11:8]));  // open: in13, in15

  assign {out_2[14:12], out_2[7:0]} = 11'h202;

  // Other names for the same wires on the sheet: func3_func7[9:0] = {inst[31:25], inst[14:12]}
endmodule

module Itype_logic (
  input  [31:0] in_1,
  output [14:0] out_2
);

  wire comparator_1_eq, comparator_2_eq, comparator_3_eq, comparator_4_eq, comparator_5_eq, comparator_6_eq,
       comparator_7_eq, comparator_8_eq;

  Comparator #(.width(3), .mode("unsigned")) comparator_1 (
    .a(in_1[14:12]), .b(3'b000), .eq(comparator_1_eq));  // open: gt, lt
  Comparator #(.width(3), .mode("unsigned")) comparator_2 (
    .a(in_1[14:12]), .b(3'b111), .eq(comparator_2_eq));  // open: gt, lt
  Comparator #(.width(3), .mode("unsigned")) comparator_3 (
    .a(in_1[14:12]), .b(3'b110), .eq(comparator_3_eq));  // open: gt, lt
  Comparator #(.width(3), .mode("unsigned")) comparator_4 (
    .a(in_1[14:12]), .b(3'b100), .eq(comparator_4_eq));  // open: gt, lt
  Comparator #(.width(10), .mode("unsigned")) comparator_5 (
    .a({in_1[31:25], in_1[14:12]}), .b(10'h5), .eq(comparator_5_eq));  // open: gt, lt
  Comparator #(.width(10), .mode("unsigned")) comparator_6 (
    .a({in_1[31:25], in_1[14:12]}), .b(10'h101), .eq(comparator_6_eq));  // open: gt, lt
  Comparator #(.width(10), .mode("unsigned")) comparator_7 (
    .a({in_1[31:25], in_1[14:12]}), .b(10'h1), .eq(comparator_7_eq));  // open: gt, lt
  Comparator #(.width(3), .mode("unsigned")) comparator_8 (
    .a(in_1[14:12]), .b(3'b010), .eq(comparator_8_eq));  // open: gt, lt
  Priority_Encoder #(.select(4)) priority_encoder_1 (
    .in0(comparator_1_eq), .in1(comparator_2_eq), .in2(comparator_3_eq), .in3(comparator_4_eq),
    .in4(comparator_5_eq), .in5(comparator_6_eq), .in6(comparator_7_eq), .in7(comparator_8_eq),
    .out(out_2[11:8]));  // open: in8, in9, in10, in11, in12, in13, in14, in15

  assign {out_2[14:12], out_2[7:0]} = 11'h282;

  // Other names for the same wires on the sheet: func3[2:0] = in_1[14:12];
  //   func3_func7[9:0] = {in_1[31:25], in_1[14:12]}
endmodule

module LItype_logic (
  input  [31:0] in_1,
  output [14:0] out_2
);


  assign out_2 = 15'h82;

  // Other names for the same wires on the sheet: func3[2:0] = in_1[14:12]
endmodule

module Stype_logic (
  input  [31:0] in_1,
  input  in_2,
  input  in_3,
  output [14:0] out_4
);

  wire comparator_1_eq, nor_1_out;

  Multiplexer #(.enable("false")) multiplexer_1 (.in0(1'b1), .in1(nor_1_out), .out(out_4[12]), .sel(comparator_1_eq));
  Comparator #(.width(3), .mode("unsigned")) comparator_1 (
    .a(in_1[14:12]), .b(3'b111), .eq(comparator_1_eq));  // open: gt, lt
  nor nor_1 (nor_1_out, in_2, in_3);

  assign {out_4[14:13], out_4[11:0]} = 14'h1084;

  // Other names for the same wires on the sheet: BrEq = in_2; BrLt = in_3; func3[2:0] = in_1[14:12]
endmodule

module SBtype_logic (
  input  [31:0] in_1,
  input  in_2,
  input  in_3,
  output [14:0] out_4
);

  wire comparator_1_eq, comparator_2_eq, comparator_3_eq, comparator_4_eq, comparator_5_eq, comparator_6_eq,
       comparator_7_eq, comparator_8_eq, comparator_9_eq, comparator_10_eq, comparator_11_eq,
       comparator_12_eq, not_1_out, not_2_out, not_3_out;
  wire [2:0] priority_encoder_1_out, priority_encoder_2_out;

  Comparator #(.width(3), .mode("unsigned")) comparator_1 (
    .a(in_1[14:12]), .b(3'b000), .eq(comparator_1_eq));  // open: gt, lt
  Comparator #(.width(3), .mode("unsigned")) comparator_2 (
    .a(in_1[14:12]), .b(3'b001), .eq(comparator_2_eq));  // open: gt, lt
  Comparator #(.width(3), .mode("unsigned")) comparator_3 (
    .a(in_1[14:12]), .b(3'b100), .eq(comparator_3_eq));  // open: gt, lt
  Comparator #(.width(3), .mode("unsigned")) comparator_4 (
    .a(in_1[14:12]), .b(3'b101), .eq(comparator_4_eq));  // open: gt, lt
  Comparator #(.width(3), .mode("unsigned")) comparator_5 (
    .a(in_1[14:12]), .b(3'b110), .eq(comparator_5_eq));  // open: gt, lt
  Comparator #(.width(3), .mode("unsigned")) comparator_6 (
    .a(in_1[14:12]), .b(3'b111), .eq(comparator_6_eq));  // open: gt, lt
  Comparator #(.width(3), .mode("unsigned")) comparator_7 (
    .a(in_1[14:12]), .b(3'b000), .eq(comparator_7_eq));  // open: gt, lt
  Comparator #(.width(3), .mode("unsigned")) comparator_8 (
    .a(in_1[14:12]), .b(3'b001), .eq(comparator_8_eq));  // open: gt, lt
  Comparator #(.width(3), .mode("unsigned")) comparator_9 (
    .a(in_1[14:12]), .b(3'b100), .eq(comparator_9_eq));  // open: gt, lt
  Comparator #(.width(3), .mode("unsigned")) comparator_10 (
    .a(in_1[14:12]), .b(3'b101), .eq(comparator_10_eq));  // open: gt, lt
  Comparator #(.width(3), .mode("unsigned")) comparator_11 (
    .a(in_1[14:12]), .b(3'b110), .eq(comparator_11_eq));  // open: gt, lt
  Comparator #(.width(3), .mode("unsigned")) comparator_12 (
    .a(in_1[14:12]), .b(3'b111), .eq(comparator_12_eq));  // open: gt, lt
  Priority_Encoder priority_encoder_1 (
    .in0(comparator_1_eq), .in1(comparator_2_eq), .in2(comparator_3_eq), .in3(comparator_4_eq),
    .in4(comparator_5_eq), .in5(comparator_6_eq), .out(priority_encoder_1_out));  // open: in6, in7, en_in
  Priority_Encoder priority_encoder_2 (
    .in0(comparator_7_eq), .in1(comparator_8_eq), .in2(comparator_9_eq), .in3(comparator_10_eq),
    .in4(comparator_11_eq), .in5(comparator_12_eq), .out(priority_encoder_2_out));  // open: in6, in7, en_in
  Multiplexer #(.select(3), .enable("false")) multiplexer_1 (
    .in0(1'b0), .in1(1'b0), .in2(1'b0), .in3(1'b0), .in4(1'b1), .in5(1'b1), .out(out_4[5]),
    .sel(priority_encoder_2_out));  // open: in6, in7
  Multiplexer #(.select(3), .enable("false")) multiplexer_2 (
    .in0(in_2), .in1(not_1_out), .in2(in_3), .in3(not_2_out), .in4(in_3), .in5(not_3_out), .out(out_4[0]),
    .sel(priority_encoder_1_out));  // open: in6, in7
  not not_1 (not_1_out, in_2);
  not not_2 (not_2_out, in_3);
  not not_3 (not_3_out, in_3);

  assign {out_4[14:6], out_4[4:1]} = 13'h834;

  // Other names for the same wires on the sheet: BrEq = in_2; BrLt = in_3; func3[2:0] = in_1[14:12]; PCSel = out_4[0];
  //   BrUn = out_4[5]
endmodule

module U1type_logic (
  output [14:0] out_1
);


  assign out_1 = 15'h20ce;
endmodule

module U2type_logic (
  output [14:0] out_1
);


  assign out_1 = 15'h2dce;
endmodule

module UJtype_logic (
  output [14:0] out_1
);


  assign out_1 = 15'h40d3;
endmodule

module jalr_logic (
  output [14:0] out_1
);


  assign out_1 = 15'h4083;
endmodule
