// Logisim project cpu.circ as structural Verilog: 3 circuits, main circuit main
module main (
  input  [31:0] INSTRUCTION,
  input  CLOCK,
  output [31:0] PROGRAM_COUNTER,
  output [31:0] ra,
  output [31:0] sp,
  output [31:0] t0,
  output [31:0] t1,
  output [31:0] t2,
  output [31:0] s0,
  output [31:0] s1,
  output [31:0] a0
);

  wire branch_comp_1_breq, branch_comp_1_brlt, control_logic_1_asel, control_logic_1_brun,
       control_logic_1_bsel, control_logic_1_memrw, control_logic_1_pcsel, control_logic_1_regwen, l_ps,
       swlt_set_1_cmpset, undriven;
  wire [1:0] control_logic_1_wbsel;
  wire [2:0] control_logic_1_immsel;
  wire [3:0] control_logic_1_alusel;
  wire [31:0] adder_1_out, adder_2_out, alu, DMEM_p5, imm_gen_1_imm, INS_OUT, IReg_q, mem_out_1_outputdata,
       multiplexer_1_out, multiplexer_3_out, multiplexer_4_out, multiplexer_5_out, multiplexer_6_out,
       PRESENT_PC, RegFile_read_data_1, RegFile_read_data_2, wb;

  Adder #(.width(32)) adder_1 (.a(PROGRAM_COUNTER), .b(32'h4), .out(adder_1_out));  // open: cin, cout
  Register #(.width(32)) PC (.D(multiplexer_1_out), .clk(CLOCK), .Q(PROGRAM_COUNTER));  // open: en, clr
  Multiplexer #(.width(32), .enable("false")) multiplexer_1 (
    .in0(adder_1_out), .in1(alu), .out(multiplexer_1_out), .sel(control_logic_1_pcsel));
  Register #(.width(1)) register_1 (.D(control_logic_1_pcsel), .clk(CLOCK), .Q(l_ps));  // open: en, clr
  control_logic control_logic_1 (
    .BSel(control_logic_1_bsel), .RegWEn(control_logic_1_regwen), .ASel(control_logic_1_asel),
    .ImmSel(control_logic_1_immsel), .BrUn(control_logic_1_brun), .PCSel(control_logic_1_pcsel),
    .BrLt(branch_comp_1_brlt), .BrEq(branch_comp_1_breq), .inst(INS_OUT), .ALUSel(control_logic_1_alusel),
    .MemRW(control_logic_1_memrw), .WBSel(control_logic_1_wbsel));
  Register #(.width(32)) IReg (.D(INSTRUCTION), .clk(CLOCK), .Q(IReg_q), .clr(undriven));  // open: en
  Register #(.width(32)) register_2 (.D(PROGRAM_COUNTER), .clk(CLOCK), .Q(PRESENT_PC));  // open: en, clr
  imm_gen imm_gen_1 (.ImmSel(control_logic_1_immsel), .imm(imm_gen_1_imm), .inst(INS_OUT));
  Multiplexer #(.width(32), .enable("false")) multiplexer_2 (.in0(IReg_q), .in1({32{1'b0}}), .out(INS_OUT), .sel(l_ps));
  regfile_main RegFile (
    .rs2(INS_OUT[24:20]), .rd(INS_OUT[11:7]), .Read_Data_1(RegFile_read_data_1),
    .Read_Data_2(RegFile_read_data_2), .ra(ra), .sp(sp), .t0(t0), .t1(t1), .t2(t2), .s0(s0), .s1(s1),
    .a0(a0), .rs1(INS_OUT[19:15]), .Write_Data(wb), .RegWEn(control_logic_1_regwen), .clk(CLOCK));
  Multiplexer #(.width(32), .enable("false")) multiplexer_3 (
    .in0(RegFile_read_data_1), .in1(imm_gen_1_imm), .out(multiplexer_3_out), .sel(swlt_set_1_cmpset));
  swlt_set swlt_set_1 (.inst(INS_OUT), .cmpSet(swlt_set_1_cmpset));
  Multiplexer #(.width(32), .enable("false")) multiplexer_4 (
    .in0(imm_gen_1_imm), .in1({32{1'b0}}), .out(multiplexer_4_out), .sel(swlt_set_1_cmpset));
  branch_comp branch_comp_1 (
    .BrEq(branch_comp_1_breq), .BrUn(control_logic_1_brun), .rs1(multiplexer_3_out),
    .BrLt(branch_comp_1_brlt), .rs2(RegFile_read_data_2));
  Multiplexer #(.width(32), .enable("false")) multiplexer_5 (
    .in0(RegFile_read_data_1), .in1(PRESENT_PC), .out(multiplexer_5_out), .sel(control_logic_1_asel));
  Multiplexer #(.width(32), .enable("false")) multiplexer_6 (
    .in0(RegFile_read_data_2), .in1(multiplexer_4_out), .out(multiplexer_6_out), .sel(control_logic_1_bsel));
  alu Arithmetic_Logic_Unit (
    .ALUSel(control_logic_1_alusel), .Result(alu), .A(multiplexer_5_out), .B(multiplexer_6_out));
  // mem_main DMEM: pin names not known; wires that end beside it: alu, RegFile_read_data_2, CLOCK, control_logic_1_memrw, DMEM_p5
  mem_out mem_out_1 (.inst(INS_OUT), .InputData(DMEM_p5), .OutputData(mem_out_1_outputdata));
  Adder #(.width(32)) adder_2 (.a(PRESENT_PC), .b(32'h4), .out(adder_2_out));  // open: cin, cout
  Multiplexer #(.select(2), .width(32), .enable("false")) multiplexer_7 (
    .in0(mem_out_1_outputdata), .in1(alu), .in2(adder_2_out), .out(wb), .sel(control_logic_1_wbsel));  // open: in3

  // Other names for the same wires on the sheet: clk = CLOCK

  // Notes on the sheet:
  //   Output
  //   IMEM (do **NOT** move this)
  //   Inputs
  //   It is OK to move the PC, RegFile, ALU, MEM, Branch Comp, Imm Gen, and Control Logic to wherever is most convenient for you when constructing your CPU, and to delete this text
  //   Inputs/Outputs for testing. Do **NOT** move these.
endmodule

module mem_out (
  input  [31:0] inst,
  input  [31:0] InputData,
  output [31:0] OutputData
);

  wire comparator_1_eq, comparator_2_eq;
  wire [1:0] priority_encoder_1_out;
  wire [31:0] bit_extender_1_out, bit_extender_2_out;

  Comparator #(.width(10), .mode("unsigned")) comparator_1 (
    .a({inst[14:12], inst[6:0]}), .b(10'h3), .eq(comparator_1_eq));  // open: gt, lt
  Comparator #(.width(10), .mode("unsigned")) comparator_2 (
    .a({inst[14:12], inst[6:0]}), .b(10'h83), .eq(comparator_2_eq));  // open: gt, lt
  Priority_Encoder #(.select(2)) priority_encoder_1 (
    .in0(1'b1), .in1(comparator_1_eq), .in2(comparator_2_eq), .out(priority_encoder_1_out));  // open: in3
  assign bit_extender_1_out = {{24{InputData[7]}}, InputData[7:0]};  // Bit_Extender bit_extender_1
  assign bit_extender_2_out = {{16{InputData[15]}}, InputData[15:0]};  // Bit_Extender bit_extender_2
  Multiplexer #(.select(2), .width(32), .enable("false")) multiplexer_1 (
    .in0(InputData), .in1(bit_extender_1_out), .in2(bit_extender_2_out), .out(OutputData),
    .sel(priority_encoder_1_out));  // open: in3

  // Other names for the same wires on the sheet: data[31:0] = InputData; func3_opcode[9:0] = {inst[14:12], inst[6:0]}
endmodule

module swlt_set (
  input  [31:0] inst,
  output cmpSet
);

  Comparator #(.width(10)) comparator_1 (.a({inst[14:12], inst[6:0]}), .b(10'h3a3), .eq(cmpSet));  // open: gt, lt

  // Other names for the same wires on the sheet: func3_opcode[9:0] = {inst[14:12], inst[6:0]}
endmodule
