// Logisim project regfile.circ as structural Verilog: 1 circuit, main circuit main
module main (
  input  [4:0] rs1,
  input  [4:0] rs2,
  input  [4:0] rd,
  input  [31:0] Write_Data,
  input  RegWEn,
  input  clk,
  output [31:0] ra,
  output [31:0] sp,
  output [31:0] t0,
  output [31:0] t1,
  output [31:0] t2,
  output [31:0] s0,
  output [31:0] s1,
  output [31:0] a0,
  output [31:0] Read_Data_1,
  output [31:0] Read_Data_2
);

  wire x1_WEn, x2_WEn, x5_WEn, x6_WEn, x7_WEn, x8_WEn, x9_WEn, x10_WEn;

  Register #(.width(32)) x1_ra (.D(Write_Data), .en(x1_WEn), .clk(clk), .Q(ra));  // open: clr
  Register #(.width(32)) x7_t2 (.D(Write_Data), .en(x7_WEn), .clk(clk), .Q(t2));  // open: clr
  Demultiplexer #(.select(5), .enable("false")) demultiplexer_1 (
    .out1(x1_WEn), .out2(x2_WEn), .out5(x5_WEn), .out6(x6_WEn), .out7(x7_WEn), .out8(x8_WEn), .out9(x9_WEn),
    .out10(x10_WEn), .in(RegWEn), .sel(rd));  // open: out0, out3, out4, out11, out12, out13, out14, out15, out16, out17, out18, out19, out20, out21, out22, out23, out24, out25, out26, out27, out28, out29, out30, out31
  Register #(.width(32)) x2_sp (.D(Write_Data), .en(x2_WEn), .clk(clk), .Q(sp));  // open: clr
  Register #(.width(32)) x8_s0 (.D(Write_Data), .en(x8_WEn), .clk(clk), .Q(s0));  // open: clr
  Register #(.width(32)) x5_t0 (.D(Write_Data), .en(x5_WEn), .clk(clk), .Q(t0));  // open: clr
  Register #(.width(32)) x9_s1 (.D(Write_Data), .en(x9_WEn), .clk(clk), .Q(s1));  // open: clr
  Multiplexer #(.select(5), .width(32), .enable("false")) multiplexer_1 (
    .in0({32{1'b0}}), .in1(ra), .in2(sp), .in5(t0), .in6(t1), .in7(t2), .in8(s0), .in9(s1), .in10(a0),
    .out(Read_Data_1), .sel(rs1));  // open: in3, in4, in11, in12, in13, in14, in15, in16, in17, in18, in19, in20, in21, in22, in23, in24, in25, in26, in27, in28, in29, in30, in31
  Register #(.width(32)) x6_t1 (.D(Write_Data), .en(x6_WEn), .clk(clk), .Q(t1));  // open: clr
  Register #(.width(32)) x10_a0 (.D(Write_Data), .en(x10_WEn), .clk(clk), .Q(a0));  // open: clr
  Multiplexer #(.select(5), .width(32), .enable("false")) multiplexer_2 (
    .in0({32{1'b0}}), .in1(ra), .in2(sp), .in5(t0), .in6(t1), .in7(t2), .in8(s0), .in9(s1), .in10(a0),
    .out(Read_Data_2), .sel(rs2));  // open: in3, in4, in11, in12, in13, in14, in15, in16, in17, in18, in19, in20, in21, in22, in23, in24, in25, in26, in27, in28, in29, in30, in31

  // Other names for the same wires on the sheet: read_data1[31:0] = Read_Data_1; read_data2[31:0] = Read_Data_2;
  //   read_reg1[4:0] = rs1; read_reg2[4:0] = rs2; write_en = RegWEn; write_reg[4:0] = rd

  // Notes on the sheet:
  //   INPUTS to your circuit
  //   DON'T CHANGE THE LOCATIONS OF THE INPUTS AND OUTPUTS!
  //   These are DEBUG/TEST outputs from your circuit.
  //   OUTPUTS from your circuit
endmodule
